// Logisim project ALU.circ as structural Verilog: 3 circuits, main circuit ALU
module ALU (
  input  Cin,
  input  [3:0] A3A2A1A0,
  input  [3:0] B3B2B1B0,
  input  [1:0] S1S0,
  input  [1:0] S3S2,
  output Cout,
  output [3:0] F3F2F1F0
);

  wire [3:0] arithmethic_unit_1_d3d2d1d0, LU_e3e2e1e0;

  arithmethic_unit arithmethic_unit_1 (
    .A3A2A1A0(A3A2A1A0), .B3B2B1B0(B3B2B1B0), .CIn(Cin), .S1S0(S1S0), .D3D2D1D0(arithmethic_unit_1_d3d2d1d0),
    .carry(Cout));
  Logical_unit LU (.A3A2A1A0(A3A2A1A0), .B3B2B1B0(B3B2B1B0), .S1S0(S1S0), .E3E2E1E0(LU_e3e2e1e0));
  Multiplexer #(.select(2), .width(4), .disabled(0), .enable("false")) multiplexer_1 (
    .in0(arithmethic_unit_1_d3d2d1d0), .in1(LU_e3e2e1e0), .out(F3F2F1F0), .sel(S3S2));  // open: in2, in3

  // Notes on the sheet:
  //   DHRUV PUVAR - 20CE117
endmodule

module arithmethic_unit (
  input  CIn,
  input  [3:0] A3A2A1A0,
  input  [3:0] B3B2B1B0,
  input  [1:0] S1S0,
  output [3:0] D3D2D1D0,
  output carry
);

  wire [3:0] multiplexer_1_out, not_1_out, not_2_out;

  assign not_1_out = ~B3B2B1B0;  // NOT_Gate not_1, 4 bits wide
  assign not_2_out = ~4'b0000;  // NOT_Gate not_2, 4 bits wide
  Multiplexer #(.select(2), .width(4), .disabled(0), .enable("false")) multiplexer_1 (
    .in0(B3B2B1B0), .in1(not_1_out), .in2(4'b0000), .in3(not_2_out), .out(multiplexer_1_out), .sel(S1S0));
  Adder #(.width(4)) adder_1 (.a(A3A2A1A0), .b(multiplexer_1_out), .out(D3D2D1D0), .cin(CIn), .cout(carry));
endmodule

module Logical_unit (
  input  [3:0] A3A2A1A0,
  input  [3:0] B3B2B1B0,
  input  [1:0] S1S0,
  output [3:0] E3E2E1E0
);

  wire [3:0] AND_out, NOT_out, OR_out, XOR_out;

  assign NOT_out = ~A3A2A1A0;  // NOT_Gate NOT, 4 bits wide
  assign AND_out = A3A2A1A0 & B3B2B1B0;  // AND_Gate AND, 4 bits wide
  assign OR_out = A3A2A1A0 | B3B2B1B0;  // OR_Gate OR, 4 bits wide
  assign XOR_out = A3A2A1A0 ^ B3B2B1B0;  // XOR_Gate XOR, 4 bits wide
  Multiplexer #(.select(2), .width(4), .disabled(0), .enable("false")) multiplexer_1 (
    .in0(AND_out), .in1(OR_out), .in2(XOR_out), .in3(NOT_out), .out(E3E2E1E0), .sel(S1S0));
endmodule
