// Logisim project Addition and subtraction using signed magnitude--pr4.circ as structural Verilog: 2 circuits, main circuit + , - sign bits
module sign_bits (
  input  _0___Addition,
  input  A,
  input  B,
  input  [2:0] Bs,
  input  [2:0] in_5,
  input  in_6,
  output [2:0] out_7,
  output As,
  output [2:0] A_2,
  output [2:0] A_3,
  output As_2,
  output [2:0] A_4,
  output As_3,
  output [2:0] A_5,
  output As_4
);

  wire adder_1_cout, adder_3_cout, comparator_1_eq, comparator_1_gt, comparator_1_lt, not_2_out, not_5_out,
       not_6_out, or_1_out, or_2_out, xor_1_out, xor_2_out;
  wire [2:0] adder_1_out, adder_3_out, controlled_buffer_1_out, controlled_buffer_3_out,
       controlled_buffer_8_out, not_1_out, not_3_out;

  assign not_1_out = ~out_7;  // NOT_Gate not_1, 3 bits wide
  assign controlled_buffer_1_out = not_2_out ? not_1_out : 3'bz;  // Controlled_Buffer controlled_buffer_1
  not not_2 (not_2_out, adder_1_cout);
  Adder #(.width(3)) adder_1 (.a(not_3_out), .b(Bs), .out(adder_1_out), .cin(1'b1), .cout(adder_1_cout));
  Adder #(.width(3)) adder_2 (.a(controlled_buffer_1_out), .b(3'b001), .out(A_2));  // open: cin, cout
  assign not_3_out = ~in_5;  // NOT_Gate not_3, 3 bits wide
  assign out_7 = xor_2_out ? adder_1_out : 3'bz;  // Controlled_Buffer controlled_buffer_2
  not not_4 (As, A);
  Comparator #(.width(3)) comparator_1 (
    .a(controlled_buffer_3_out), .b(3'b000), .gt(comparator_1_gt), .eq(comparator_1_eq), .lt(comparator_1_lt));
  assign controlled_buffer_3_out = adder_1_cout ? out_7 : 3'bz;  // Controlled_Buffer controlled_buffer_3
  or or_1 (or_1_out, comparator_1_gt, comparator_1_lt);
  assign A_4 = or_2_out ? controlled_buffer_3_out : 3'bz;  // Controlled_Buffer controlled_buffer_4
  or or_2 (or_2_out, comparator_1_gt, comparator_1_lt);
  assign A_5 = comparator_1_eq ? controlled_buffer_3_out : 3'bz;  // Controlled_Buffer controlled_buffer_5
  assign As_4 = comparator_1_eq ? in_6 : 1'bz;  // Controlled_Buffer controlled_buffer_6
  assign As_3 = or_1_out ? A : 1'bz;  // Controlled_Buffer controlled_buffer_7
  Adder #(.width(3)) adder_3 (.a(in_5), .b(Bs), .out(adder_3_out), .cout(adder_3_cout));  // open: cin
  assign controlled_buffer_8_out = not_6_out ? adder_3_out : 3'bz;  // Controlled_Buffer controlled_buffer_8
  not not_5 (not_5_out, adder_3_cout);
  assign A_3 = not_5_out ? controlled_buffer_8_out : 3'bz;  // Controlled_Buffer controlled_buffer_9
  LED led_1 (.in(adder_3_cout));
  xor xor_1 (xor_1_out, A, B);
  xor xor_2 (xor_2_out, xor_1_out, _0___Addition);
  not not_6 (not_6_out, xor_2_out);

  assign As_2 = A;

  // Notes on the sheet:
  //   DHRUV PUVAR and 20CE117
  //   A<B
  //   Subtraction
  //   As
  //   A>B
  //   A=0
  //   Addition
  //   Overflow
  //   1 - Subtraction
endmodule

module Main (
);

  sign_bits sign_bits_1 ();  // open: in_6, Bs, in_5, A, B, _0___Addition, out_7, As, A_2, A_3, As_2, A_4, As_3, A_5, As_4
endmodule
