// Logisim project Addition using signed magnitude.circ as structural Verilog: 1 circuit, main circuit main
module main (
  input  As,
  input  Bs,
  input  [2:0] A,
  input  [2:0] B,
  input  in_5,
  input  in_6,
  input  [2:0] in_7,
  input  [2:0] in_8,
  input  in_9,
  output [2:0] out_10,
  output out_11,
  output [2:0] A_2,
  output As_2,
  output As_3,
  output [2:0] A_3,
  output [2:0] A_4,
  output As_4,
  output [2:0] A_5,
  output As_5
);

  wire adder_1_cout, comparator_1_eq, comparator_1_gt, comparator_1_lt, not_2_out, not_5_out, or_1_out;
  wire [2:0] adder_1_out, adder_3_out, controlled_buffer_1_out, controlled_buffer_3_out, not_1_out, not_4_out;

  assign not_1_out = ~out_10;  // NOT_Gate not_1, 3 bits wide
  assign controlled_buffer_1_out = not_2_out ? not_1_out : 3'bz;  // Controlled_Buffer controlled_buffer_1
  not not_2 (not_2_out, adder_1_cout);
  Adder #(.width(3)) adder_1 (.a(not_4_out), .b(A), .out(adder_1_out), .cin(in_5), .cout(adder_1_cout));
  not not_3 (As_3, As);
  Adder #(.width(3)) adder_2 (.a(controlled_buffer_1_out), .b(in_7), .out(A_3));  // open: cin, cout
  assign not_4_out = ~B;  // NOT_Gate not_4, 3 bits wide
  assign out_10 = out_11 ? adder_1_out : 3'bz;  // Controlled_Buffer controlled_buffer_2
  Comparator #(.width(3)) comparator_1 (
    .a(controlled_buffer_3_out), .b(in_8), .gt(comparator_1_gt), .eq(comparator_1_eq), .lt(comparator_1_lt));
  assign controlled_buffer_3_out = adder_1_cout ? out_10 : 3'bz;  // Controlled_Buffer controlled_buffer_3
  assign A_4 = or_1_out ? controlled_buffer_3_out : 3'bz;  // Controlled_Buffer controlled_buffer_4
  or or_1 (or_1_out, comparator_1_gt, comparator_1_lt);
  assign A_5 = comparator_1_eq ? controlled_buffer_3_out : 3'bz;  // Controlled_Buffer controlled_buffer_5
  Adder #(.width(3)) adder_3 (.a(B), .b(A), .out(adder_3_out), .cin(in_6));  // open: cout
  assign A_2 = not_5_out ? adder_3_out : 3'bz;  // Controlled_Buffer controlled_buffer_6
  xor xor_1 (out_11, As, Bs);
  not not_5 (not_5_out, out_11);

  assign As_2 = As;
  assign As_4 = As;
  assign As_5 = in_9;

  // Notes on the sheet:
  //   A<B
  //   A>B
  //   A=0
  //   Subtraction
  //   Addition
endmodule
